// Logisim project s-mips.circ as structural Verilog
module S_MIPS_Board (
  input  DESHABILITAR_DISPATCHER,
  output halt
);

  wire button_1_out, CLK, CS, d_ff_1_q, LCLR, LoadRAM, LoadRAMOn, LW, R_R_W, R_W, ram_dispatcher_1_finished,
       RCS, Reset_out, RST, TTY_EN;
  wire [2:0] KDB;
  wire [3:0] LMask, Mask, ram_1_read_time, ram_1_write_time, RMask;
  wire [6:0] KDB_DATA, TTY_DATA;
  wire [15:0] Addr, LAddr, RAddr;
  wire [31:0] I0, I1, I2, I3, LData, ram_1_data_out_0, ram_1_data_out_1, ram_1_data_out_2, ram_1_data_out_3,
       RI0, RI1, RI2, RI3;

  TTY #(.rows(25), .cols(80)) tty_1 (.data(TTY_DATA), .clk(CLK), .we(TTY_EN), .clr(RST));
  not not_1 (LoadRAMOn, ram_dispatcher_1_finished);
  RAM_Dispatcher ram_dispatcher_1 (
    .WriteTime(ram_1_write_time), .Clock(CLK), .Data(LData), .Address(LAddr), .Mask(LMask),
    .Finished(ram_dispatcher_1_finished), .Write(LW), .CLR(LCLR));
  Keyboard #(.buflen(64)) keyboard_1 (.clk(CLK), .re(KDB[0]), .avail(KDB[2]), .data(KDB_DATA));  // open: clr
  RAM ram_1 (
    .Address(RAddr), .Data_Out_0(ram_1_data_out_0), .Data_Out_1(ram_1_data_out_1),
    .Data_Out_2(ram_1_data_out_2), .Data_Out_3(ram_1_data_out_3), .Data_In_0(RI0), .Data_In_1(RI1),
    .Data_In_2(RI2), .Data_In_3(RI3), .Mask(RMask), .nRead_Write(R_R_W), .Chip_Select(RCS),
    .Read_Time(ram_1_read_time), .Reset(button_1_out), .Write_Time(ram_1_write_time));
  Button button_1 (.out(button_1_out));
  D_Flip_Flop d_ff_1 (.clk(CLK), .D(1'b1), .Q(d_ff_1_q), .reset(Reset_out));  // open: Qn, preset, en
  Button Reset (.out(Reset_out));
  S_MIPS s_mips_1 (
    .Kbd_Enable(KDB[0]), .Address(Addr), .Kbd_Clear(KDB[1]), .Kbd_Available(KDB[2]), .RAM_In_0(I0),
    .Kbd_ASCII_Data(KDB_DATA), .RAM_In_1(I1), .TTY_Enable(TTY_EN), .RAM_In_2(I2), .RAM_In_3(I3),
    .TTY_ASCII_Data(TTY_DATA), .Reset(RST), .RAM_Out_0(ram_1_data_out_0), .Clock(CLK),
    .RAM_Out_1(ram_1_data_out_1), .Stop(halt), .RAM_Out_2(ram_1_data_out_2), .RAM_Out_3(ram_1_data_out_3),
    .Mask(Mask), .Read_Time(ram_1_read_time), .Write_Time(ram_1_write_time), .nRead_Write(R_W),
    .Chip_Select(CS));
  D_Flip_Flop d_ff_2 (.clk(CLK), .D(d_ff_1_q), .Qn(LCLR), .reset(Reset_out));  // open: Q, preset, en
  or or_1 (RST, LCLR, LoadRAM);
  Clock clock_1 (.out(CLK));
  Multiplexer #(.width(32), .enable("false")) multiplexer_1 (.in0(I0), .in1(LData), .out(RI0), .sel(LoadRAM));
  Multiplexer #(.width(32), .enable("false")) multiplexer_2 (.in0(I1), .in1(LData), .out(RI1), .sel(LoadRAM));
  Multiplexer #(.width(32), .enable("false")) multiplexer_3 (.in0(I2), .in1(LData), .out(RI2), .sel(LoadRAM));
  Multiplexer #(.width(32), .enable("false")) multiplexer_4 (.in0(I3), .in1(LData), .out(RI3), .sel(LoadRAM));
  and and_1 (LoadRAM, ~DESHABILITAR_DISPATCHER, LoadRAMOn);  // AND_Gate
  Multiplexer #(.width(16), .enable("false")) multiplexer_5 (.in0(Addr), .in1(LAddr), .out(RAddr), .sel(LoadRAM));
  Multiplexer #(.width(4), .enable("false")) multiplexer_6 (.in0(Mask), .in1(LMask), .out(RMask), .sel(LoadRAM));
  Multiplexer #(.enable("false")) multiplexer_7 (.in0(CS), .in1(LW), .out(RCS), .sel(LoadRAM));
  Multiplexer #(.enable("false")) multiplexer_8 (.in0(R_W), .in1(LW), .out(R_R_W), .sel(LoadRAM));

  // Notes on the sheet:
  //   NO MODIFICAR
  //   Keyboard
endmodule

module RAM (
  input  [15:0] Address,
  input  [31:0] Data_In_0,
  input  [31:0] Data_In_1,
  input  [31:0] Data_In_2,
  input  [31:0] Data_In_3,
  input  [3:0] Mask,
  input  nRead_Write,
  input  Chip_Select,
  input  Reset,
  output [31:0] Data_Out_0,
  output [31:0] Data_Out_1,
  output [31:0] Data_Out_2,
  output [31:0] Data_Out_3,
  output [3:0] Read_Time,
  output [3:0] Write_Time
);

  wire and_2_out, and_3_out, and_4_out, and_5_out, and_6_out, and_7_out, and_8_out, and_9_out, Changed, CLK,
       comparator_2_eq, comparator_3_eq, comparator_4_eq, comparator_5_eq, comparator_6_eq, Count,
       demultiplexer_3_out0, Idle, Idle_q, Load, Load0, Load1, nand_1_out, or_1_out, or_2_out, or_3_out,
       or_4_out, or_5_out, or_6_out, or_7_out, or_8_out, or_9_out, or_10_out, Proc_q, Update_Mem, Zero_Time;
  wire [3:0] counter_1_q, multiplexer_1_out, subtractor_1_out;
  wire [31:0] register_1_q, register_2_q, register_3_q, register_4_q, register_5_q;

  // Probe on 4'b0011
  // Probe on 4'b0010
  Multiplexer #(.width(4), .enable("false")) multiplexer_1 (
    .in0(4'b0011), .in1(4'b0010), .out(multiplexer_1_out), .sel(nRead_Write));
  or or_1 (or_1_out, Idle, Update_Mem);
  or or_2 (or_2_out, ~Chip_Select, Reset);  // OR_Gate
  Subtractor #(.width(4)) subtractor_1 (.a(multiplexer_1_out), .b(4'b0010), .out(subtractor_1_out));  // open: bin, bout
  Demultiplexer #(.enable("false")) demultiplexer_1 (.out0(Idle), .out1(Load0), .in(Idle_q), .sel(Changed));
  D_Flip_Flop u_Idle (.clk(CLK), .D(or_1_out), .Q(Idle_q), .preset(or_2_out));  // open: Qn, en, reset
  // Probe on counter_1_q
  Counter #(.width(4), .max('hf)) counter_1 (
    .load(Load), .D(subtractor_1_out), .count(Count), .Q(counter_1_q), .clk(CLK), .clr(or_3_out));  // open: carry
  or or_3 (or_3_out, ~Chip_Select, Reset);  // OR_Gate
  Comparator #(.width(4), .mode("unsigned")) comparator_1 (
    .a(4'b0000), .b(counter_1_q), .eq(Zero_Time));  // open: gt, lt
  or or_4 (or_4_out, Count, Load0, Load1);
  Register #(.width(32)) register_1 (.D(Data_In_0), .en(Chip_Select), .Q(register_1_q), .clk(CLK), .clr(or_5_out));
  or or_5 (or_5_out, ~Chip_Select, Reset);  // OR_Gate
  Register #(.width(32)) register_2 (.D(Data_In_1), .en(Chip_Select), .Q(register_2_q), .clk(CLK), .clr(or_6_out));
  or or_6 (or_6_out, ~Chip_Select, Reset);  // OR_Gate
  Register #(.width(32)) register_3 (.D(Data_In_2), .en(Chip_Select), .Q(register_3_q), .clk(CLK), .clr(or_7_out));
  or or_7 (or_7_out, ~Chip_Select, Reset);  // OR_Gate
  Register #(.width(32)) register_4 (.D(Data_In_3), .en(Chip_Select), .Q(register_4_q), .clk(CLK), .clr(or_8_out));
  or or_8 (or_8_out, ~Chip_Select, Reset);  // OR_Gate
  Register #(.width(32)) register_5 (
    .D({{11{1'b1}}, nRead_Write, Mask, Address}), .en(Chip_Select), .Q(register_5_q), .clk(CLK),
    .clr(or_9_out));
  or or_9 (or_9_out, ~Chip_Select, Reset);  // OR_Gate
  D_Flip_Flop Proc (.clk(CLK), .D(or_4_out), .Q(Proc_q), .reset(or_10_out));  // open: Qn, preset, en
  or or_10 (or_10_out, ~Chip_Select, Reset);  // OR_Gate
  Demultiplexer #(.enable("false")) demultiplexer_2 (
    .out0(Count), .out1(Update_Mem), .in(demultiplexer_3_out0), .sel(Zero_Time));
  Demultiplexer #(.enable("false")) demultiplexer_3 (
    .out0(demultiplexer_3_out0), .out1(Load1), .in(Proc_q), .sel(Changed));
  Clock clock_1 (.out(CLK));
  Comparator #(.width(32)) comparator_2 (.a(register_1_q), .b(Data_In_0), .eq(comparator_2_eq));  // open: gt, lt
  Comparator #(.width(32)) comparator_3 (.a(register_2_q), .b(Data_In_1), .eq(comparator_3_eq));  // open: gt, lt
  Comparator #(.width(32)) comparator_4 (.a(register_3_q), .b(Data_In_2), .eq(comparator_4_eq));  // open: gt, lt
  Comparator #(.width(32)) comparator_5 (.a(register_4_q), .b(Data_In_3), .eq(comparator_5_eq));  // open: gt, lt
  Comparator #(.width(32)) comparator_6 (
    .a(register_5_q), .b({{11{1'b1}}, nRead_Write, Mask, Address}), .eq(comparator_6_eq));  // open: gt, lt
  nand nand_1 (nand_1_out, comparator_6_eq, comparator_2_eq, comparator_3_eq, comparator_4_eq, comparator_5_eq);
  and and_1 (Changed, nand_1_out, Chip_Select);
  or or_11 (Load, Count, Load1, Load0);
  and and_2 (and_2_out, Mask[0], Update_Mem, nRead_Write);
  and and_3 (and_3_out, Mask[1], Update_Mem, nRead_Write);
  and and_4 (and_4_out, Mask[2], Update_Mem, nRead_Write);
  and and_5 (and_5_out, Mask[3], Update_Mem, nRead_Write);
  RAM_part #(.addrWidth(16), .dataWidth(32), .bus("separate")) ram_1 (
    .addr(Address), .din(Data_In_0), .data(Data_Out_0), .str(and_2_out), .sel(Chip_Select), .clk(CLK),
    .ld(and_6_out), .clr(Reset));
  and and_6 (and_6_out, ~nRead_Write, Idle);  // AND_Gate
  RAM_part #(.addrWidth(16), .dataWidth(32), .bus("separate")) ram_2 (
    .addr(Address), .din(Data_In_1), .data(Data_Out_1), .str(and_3_out), .sel(Chip_Select), .clk(CLK),
    .ld(and_7_out), .clr(Reset));
  and and_7 (and_7_out, ~nRead_Write, Idle);  // AND_Gate
  RAM_part #(.addrWidth(16), .dataWidth(32), .bus("separate")) ram_3 (
    .addr(Address), .din(Data_In_2), .data(Data_Out_2), .str(and_4_out), .sel(Chip_Select), .clk(CLK),
    .ld(and_8_out), .clr(Reset));
  and and_8 (and_8_out, ~nRead_Write, Idle);  // AND_Gate
  RAM_part #(.addrWidth(16), .dataWidth(32), .bus("separate")) ram_4 (
    .addr(Address), .din(Data_In_3), .data(Data_Out_3), .str(and_5_out), .sel(Chip_Select), .clk(CLK),
    .ld(and_9_out), .clr(Reset));
  and and_9 (and_9_out, ~nRead_Write, Idle);  // AND_Gate

  assign Read_Time = 4'b0011;
  assign Write_Time = 4'b0010;

  // Other names for the same wires on the sheet: M0 = Mask[0]; M1 = Mask[1]; M2 = Mask[2]; M3 = Mask[3];
  //   RW = nRead_Write; CLR = Reset; CS = Chip_Select; Load2 = Count

  // Notes on the sheet:
  //   NO MODIFICAR
  //   excepto quizás los valores RT y WT
  //   BANK0
  //   BANK1
  //   BANK2
  //   BANK3
endmodule

module S_MIPS (
  input  Kbd_Available,
  input  [6:0] Kbd_ASCII_Data,
  input  [31:0] RAM_Out_0,
  input  [31:0] RAM_Out_1,
  input  Reset,
  input  [31:0] RAM_Out_2,
  input  Clock,
  input  [31:0] RAM_Out_3,
  input  [3:0] Read_Time,
  input  [3:0] Write_Time,
  output Kbd_Enable,
  output [15:0] Address,
  output Kbd_Clear,
  output TTY_Enable,
  output [6:0] TTY_ASCII_Data,
  output Stop,
  output [31:0] RAM_In_0,
  output [31:0] RAM_In_1,
  output [31:0] RAM_In_2,
  output [31:0] RAM_In_3,
  output [3:0] Mask,
  output nRead_Write,
  output Chip_Select
);

  wire arit, arit_I, copia, LoadInstruction, lw, PC_enable, pila, ResultLoad, RW_REG, salto, special, sw,
       Value_Source;
  wire [1:0] AddresSource, SP_s;
  wire [2:0] DI_SEL;
  wire [5:0] func_code, op_code;
  wire [15:0] offset;
  wire [31:0] Instruction, Mem_Addres, Value;

  WriteRam writeram_1 (
    .ADDRESS(Address), .VALUE(Value), .MASK(Mask), .INPUT0(RAM_In_0), .INPUT1(RAM_In_1), .INPUT2(RAM_In_2),
    .INPUT3(RAM_In_3), .MEMORY(Mem_Addres));
  ReadInstruction readinstruction_1 (
    .RAM_DATA(Instruction), .BANK0(RAM_Out_0), .BANK1(RAM_Out_1), .BANK2(RAM_Out_2), .BANK3(RAM_Out_3),
    .MEMORY(Mem_Addres));
  // Probe on RAM_In_0
  // Probe on RAM_In_1
  // Probe on RAM_In_2
  // Probe on RAM_In_3
  // Probe on Mask
  Control_Unit_2 control_unit_1 (
    .R_Time(Read_Time), .W_time(Write_Time), .Enable_PC(PC_enable), .Clock(Clock), .Ari(arit),
    .Especial(special), .Load_Word(lw), .TTY_Enable(TTY_Enable), .Copy(copia), .Store_Word(sw),
    .WrReg(RW_REG), .Halt(Stop), .Stack(pila), .rst(Reset), .fc(func_code), .JMP(salto),
    .LOAD_RESULT(ResultLoad), .INM(arit_I), .oc(op_code), .Kbd_Enable(Kbd_Enable),
    .Enable_Instruction(LoadInstruction), .ValueSrc(Value_Source), .ADDRESSOURCE(AddresSource),
    .CS(Chip_Select), .Write(nRead_Write), .DI_SEL(DI_SEL), .SP_sel(SP_s));
  Data_Path_2 data_path_1 (
    .offset(offset), .kbd_data(Kbd_ASCII_Data), .rst(Reset), .RW_REG(RW_REG), .clk(Clock),
    .kbd_avail(Kbd_Available), .PC_Enable(PC_enable), .mem_data(Instruction), .Arit(arit),
    .Especial(special), .Load_Word(lw), .Copia(copia), .Store_Word(sw), .Pila(pila), .fc(func_code),
    .Salto(salto), .Arit_I(arit_I), .oc(op_code), .Mem_Addres(Mem_Addres), .ValueSrc(Value_Source),
    .Value(Value), .LoadResult(ResultLoad), .AddresSource(AddresSource), .LoadInstruction(LoadInstruction),
    .TTY_DAta(TTY_ASCII_Data), .DI_SEL(DI_SEL), .sp_selector(SP_s));

  assign Kbd_Clear = Reset;

  // Other names for the same wires on the sheet: CLK = Clock; CS = Chip_Select; KBD_AVAIL = Kbd_Available;
  //   CLR = Reset; KBD_CLR = Reset; KBD_DATA[6:0] = Kbd_ASCII_Data; RAM_A[15:0] = Address;
  //   RAM_INPUT_0[31:0] = RAM_In_0; RAM_INPUT_1[31:0] = RAM_In_1; RAM_INPUT_2[31:0] = RAM_In_2;
  //   RAM_INPUT_3[31:0] = RAM_In_3; RAM_MASK[3:0] = Mask; RAM_OUTPUT_0[31:0] = RAM_Out_0;
  //   RAM_OUTPUT_1[31:0] = RAM_Out_1; RAM_OUTPUT_2[31:0] = RAM_Out_2; RAM_OUTPUT_3[31:0] = RAM_Out_3;
  //   RW = nRead_Write; TTY_DATA[6:0] = TTY_ASCII_Data

  // Notes on the sheet:
  //   RAM ADDRESS
  //   DATA FROM RAM
  //   DATA TO RAM
  //   DATA WRITE MASK
  //   RAM TIMING
  //   RAM CONTROL
  //   KEYBOARD
  //   TTY
  //   SEQUENCING
endmodule

module RAM_Dispatcher (
  input  [3:0] WriteTime,
  input  Clock,
  input  CLR,
  output [31:0] Data,
  output [15:0] Address,
  output [3:0] Mask,
  output Finished,
  output Write
);

  wire demultiplexer_2_out1, demultiplexer_3_out1, End, IDLE_q, IncAddr, Load, or_1_out, or_2_out, While_q,
       WriteEnd;
  wire [3:0] counter_1_q;
  wire [31:0] CurrentAddress_q;

  Counter #(.width(32), .max('hffffffff)) CurrentAddress (
    .count(IncAddr), .Q({CurrentAddress_q[31:18], Address, CurrentAddress_q[1:0]}), .clk(Clock), .clr(CLR));  // open: load, D, carry
  or or_1 (or_1_out, IncAddr, demultiplexer_3_out1, Finished);
  D_Flip_Flop IDLE (.clk(Clock), .D(or_1_out), .Q(IDLE_q), .preset(CLR));  // open: Qn, en, reset
  Demultiplexer #(.enable("false")) demultiplexer_1 (.out0(Load), .out1(Finished), .in(IDLE_q), .sel(End));
  D_Flip_Flop While (.clk(Clock), .D(or_2_out), .Q(While_q), .reset(CLR));  // open: Qn, preset, en
  or or_2 (or_2_out, Write, Load);
  RAM_part #(.addrWidth(18), .dataWidth(32)) ram_1 (
    .addr({Address, CurrentAddress_q[1:0]}), .data(Data), .clk(Clock));  // open: sel, ld, clr
  Demultiplexer #(.enable("false")) demultiplexer_2 (
    .out0(Write), .out1(demultiplexer_2_out1), .in(While_q), .sel(WriteEnd));
  Decoder #(.select(2)) decoder_1 (
    .out0(Mask[0]), .out1(Mask[1]), .out2(Mask[2]), .out3(Mask[3]), .sel(CurrentAddress_q[1:0]));  // open: en
  Demultiplexer #(.enable("false")) demultiplexer_3 (
    .out0(IncAddr), .out1(demultiplexer_3_out1), .in(demultiplexer_2_out1), .sel(End));
  Counter #(.width(4), .max('hf)) counter_1 (
    .load(Load), .D(WriteTime), .count(Write), .Q(counter_1_q), .clk(Clock));  // open: carry, clr
  Comparator #(.width(32)) comparator_1 (.a(Data), .b({32{1'b1}}), .eq(End));  // open: gt, lt
  Comparator #(.width(4)) comparator_2 (.a(4'b0000), .b(counter_1_q), .eq(WriteEnd));  // open: gt, lt

  // Other names for the same wires on the sheet: CLK = Clock; Count = Write; WT[3:0] = WriteTime
endmodule

module Register_File_2 (
  input  MD,
  input  Reset,
  input  [31:0] DI,
  input  Clk,
  input  RW,
  input  [4:0] A,
  input  [4:0] B,
  input  [4:0] DA,
  input  [31:0] HI_value,
  input  [31:0] LO_value,
  output [31:0] HI_value_2,
  output [31:0] LO_value_2,
  output [31:0] RA,
  output [31:0] RB,
  output [31:0] Stack_Pointer
);

  wire R0, R1, R2, R3, R4, R5, R6, R7, R8, R9, R10, R11, R12, R13, R14, R15, R16, R17, R18, R19, R20, R21,
       R22, R23, R24, R25, R26, R27, R28, R29, R30, R31;
  wire [31:0] O19, OR0, OR1, OR2, OR3, OR4, OR5, OR6, OR7, OR8, OR9, OR10, OR11, OR12, OR13, OR14, OR15,
       OR16, OR17, OR18, OR19, OR20, OR21, OR22, OR23, OR24, OR25, OR26, OR27, OR28, OR29, OR30;

  Register #(.width(32)) register_1 (.D({32{1'b0}}), .Q(OR0), .clk(Clk), .clr(Reset));  // open: en
  Register #(.width(32)) register_2 (.D(DI), .en(R8), .Q(OR8), .clk(Clk), .clr(Reset));
  Register #(.width(32)) register_3 (.D(DI), .en(R16), .Q(OR16), .clk(Clk), .clr(Reset));
  Register #(.width(32)) register_4 (.D(DI), .en(R24), .Q(OR24), .clk(Clk), .clr(Reset));
  Register #(.width(32)) register_5 (.D(DI), .en(R1), .Q(OR1), .clk(Clk), .clr(Reset));
  Register #(.width(32)) register_6 (.D(DI), .en(R9), .Q(OR9), .clk(Clk), .clr(Reset));
  Register #(.width(32)) register_7 (.D(DI), .en(R17), .Q(OR17), .clk(Clk), .clr(Reset));
  Register #(.width(32)) register_8 (.D(DI), .en(R25), .Q(OR25), .clk(Clk), .clr(Reset));
  Register #(.width(32)) register_9 (.D(DI), .en(R2), .Q(OR2), .clk(Clk), .clr(Reset));
  Register #(.width(32)) register_10 (.D(DI), .en(R10), .Q(OR10), .clk(Clk), .clr(Reset));
  Register #(.width(32)) register_11 (.D(DI), .en(R18), .Q(OR18), .clk(Clk), .clr(Reset));
  Register #(.width(32)) register_12 (.D(DI), .en(R26), .Q(OR26), .clk(Clk), .clr(Reset));
  Register #(.width(32)) register_13 (.D(DI), .en(R3), .Q(OR3), .clk(Clk), .clr(Reset));
  Register #(.width(32)) register_14 (.D(DI), .en(R11), .Q(OR11), .clk(Clk), .clr(Reset));
  Register #(.width(32)) register_15 (.D(DI), .en(R19), .Q(OR19), .clk(Clk), .clr(Reset));
  Register #(.width(32)) HI (.D(HI_value), .en(MD), .Q(HI_value_2), .clk(Clk), .clr(Reset));
  Register #(.width(32)) register_16 (.D(DI), .en(R27), .Q(OR27), .clk(Clk), .clr(Reset));
  Register #(.width(32)) register_17 (.D(DI), .en(R4), .Q(OR4), .clk(Clk), .clr(Reset));
  Register #(.width(32)) register_18 (.D(DI), .en(R12), .Q(OR12), .clk(Clk), .clr(Reset));
  Register #(.width(32)) register_19 (.D(DI), .en(R20), .Q(OR20), .clk(Clk), .clr(Reset));
  Register #(.width(32)) register_20 (.D(DI), .en(R28), .Q(OR28), .clk(Clk), .clr(Reset));
  Register #(.width(32)) register_21 (.D(DI), .en(R5), .Q(OR5), .clk(Clk), .clr(Reset));
  Register #(.width(32)) register_22 (.D(DI), .en(R13), .Q(OR13), .clk(Clk), .clr(Reset));
  Register #(.width(32)) register_23 (.D(DI), .en(R21), .Q(OR21), .clk(Clk), .clr(Reset));
  Register #(.width(32)) register_24 (.D(DI), .en(R29), .Q(OR29), .clk(Clk), .clr(Reset));
  Register #(.width(32)) LO (.D(LO_value), .en(MD), .Q(LO_value_2), .clk(Clk), .clr(Reset));
  Register #(.width(32)) register_25 (.D(DI), .en(R6), .Q(OR6), .clk(Clk), .clr(Reset));
  Register #(.width(32)) register_26 (.D(DI), .en(R14), .Q(OR14), .clk(Clk), .clr(Reset));
  Register #(.width(32)) register_27 (.D(DI), .en(R22), .Q(OR22), .clk(Clk), .clr(Reset));
  Register #(.width(32)) register_28 (.D(DI), .en(R30), .Q(OR30), .clk(Clk), .clr(Reset));
  Register #(.width(32)) register_29 (.D(DI), .en(R7), .Q(OR7), .clk(Clk), .clr(Reset));
  Register #(.width(32)) register_30 (.D(DI), .en(R15), .Q(OR15), .clk(Clk), .clr(Reset));
  Register #(.width(32)) register_31 (.D(DI), .en(R23), .Q(OR23), .clk(Clk), .clr(Reset));
  Register #(.width(32)) register_32 (.D(DI), .en(R31), .Q(Stack_Pointer), .clk(Clk), .clr(Reset));
  Demultiplexer #(.select(5), .enable("false")) demultiplexer_1 (
    .out0(R0), .out1(R1), .out2(R2), .out3(R3), .out4(R4), .out5(R5), .out6(R6), .out7(R7), .out8(R8),
    .out9(R9), .out10(R10), .out11(R11), .out12(R12), .out13(R13), .out14(R14), .out15(R15), .out16(R16),
    .out17(R17), .out18(R18), .out19(R19), .out20(R20), .out21(R21), .out22(R22), .out23(R23), .out24(R24),
    .out25(R25), .out26(R26), .out27(R27), .out28(R28), .out29(R29), .out30(R30), .out31(R31), .in(RW),
    .sel(DA));
  Multiplexer #(.select(5), .width(32), .disabled(0), .enable("false")) multiplexer_1 (
    .in0({32{1'b0}}), .in1(OR1), .in2(OR2), .in3(OR3), .in4(OR4), .in5(OR5), .in6(OR6), .in7(OR7), .in8(OR8),
    .in9(OR9), .in10(OR10), .in11(OR11), .in12(OR12), .in13(OR13), .in14(OR14), .in15(OR15), .in16(OR16),
    .in17(OR17), .in18(OR18), .in19(O19), .in20(OR20), .in21(OR21), .in22(OR22), .in23(OR23), .in24(OR24),
    .in25(OR25), .in26(OR26), .in27(OR27), .in28(OR28), .in29(OR29), .in30(OR30), .in31(Stack_Pointer),
    .out(RA), .sel(A));
  // Probe on RA
  Multiplexer #(.select(5), .width(32), .disabled(0), .enable("false")) multiplexer_2 (
    .in0({32{1'b0}}), .in1(OR1), .in2(OR2), .in3(OR3), .in4(OR4), .in5(OR5), .in6(OR6), .in7(OR7), .in8(OR8),
    .in9(OR9), .in10(OR10), .in11(OR11), .in12(OR12), .in13(OR13), .in14(OR14), .in15(OR15), .in16(OR16),
    .in17(OR17), .in18(OR18), .in19(O19), .in20(OR20), .in21(OR21), .in22(OR22), .in23(OR23), .in24(OR24),
    .in25(OR25), .in26(OR26), .in27(OR27), .in28(OR28), .in29(OR29), .in30(OR30), .in31(Stack_Pointer),
    .out(RB), .sel(B));

  // Other names for the same wires on the sheet: HI_VALUE_t[31:0] = HI_value_2; LO_VALUE_t[31:0] = LO_value_2;
  //   OR31[31:0] = Stack_Pointer

  // Notes on the sheet:
  //   INPUT
  //   OUPUT
endmodule

module Data_Path_2 (
  input  LoadResult,
  input  ValueSrc,
  input  LoadInstruction,
  input  [1:0] AddresSource,
  input  [2:0] DI_SEL,
  input  [15:0] offset,
  input  RW_REG,
  input  [1:0] sp_selector,
  input  clk,
  input  [6:0] kbd_data,
  input  rst,
  input  kbd_avail,
  input  [31:0] mem_data,
  input  PC_Enable,
  output Arit,
  output Especial,
  output Copia,
  output Load_Word,
  output Pila,
  output Store_Word,
  output Salto,
  output [5:0] fc,
  output Arit_I,
  output [5:0] oc,
  output [31:0] Value,
  output [6:0] TTY_DAta,
  output [31:0] Mem_Addres
);

  wire add, addi, \and , andi, beq, bgtz, blez, bltz, bne, brf, dif, div, divu, en_md, halt, j, jr, kbd_t,
       mfhi, mflo, mult, mulu, nop, \nor , \or , or_3_out, ori, pop, push, rnd_t, SF, slt, slti, sltiu, sltu,
       sub, sum, sumi, tty, \xor , xori, ZF;
  wire [1:0] or_4_out;
  wire [3:0] ALU_Selector;
  wire [4:0] DA, rd, rs, rt;
  wire [25:0] target;
  wire [31:0] alu_1_result, B, bit_extender_1_out, bit_extender_2_out, branch_control_1_pc_out, Data, DI,
       Hi_in, Hi_out, KBD, Lo_out, multiplexer_4_out, multiplexer_5_out, PC_prime, register_1_q, resultALU,
       RND, SP;
  wire [31:7] A;

  Program_Counter program_counter_1 (
    .in_1(branch_control_1_pc_out), .out_5(PC_prime), .clk(clk), .reset(rst), .enable(PC_Enable));
  // Probe on PC_prime
  assign bit_extender_1_out = {{25{1'b0}}, kbd_data};  // Bit_Extender bit_extender_1
  Multiplexer #(.width(32), .enable("false")) multiplexer_1 (
    .in0({32{1'b1}}), .in1(bit_extender_1_out), .out(KBD), .sel(kbd_avail));
  // Probe on DA
  Multiplexer #(.select(2), .width(5), .enable("false")) multiplexer_2 (
    .in0(rd), .in1(rt), .in2({5{1'b1}}), .out(DA), .sel(sp_selector));  // open: in3
  // Probe on sp_selector
  Random #(.width(32)) u_RND (.clk(clk), .out(RND));  // open: next, clr
  Branch_Control branch_control_1 (
    .bne(bne), .blez(blez), .bgtz(bgtz), .bltz(bltz), .ZF(ZF), .NF(SF), .j(j), .jr(jr), .beq(beq),
    .rs({A, TTY_DAta}), .pc_in(PC_prime), .offset(offset), .target(target), .pc_out(branch_control_1_pc_out),
    .Is_Branch_flag(brf));
  // Probe on branch_control_1_pc_out
  // Probe on DI
  or or_1 (en_md, mult, mulu, div, divu);
  Multiplexer #(.select(3), .width(32), .enable("false")) multiplexer_3 (
    .in0(resultALU), .in1(Data), .in2(Hi_out), .in3(Lo_out), .in4(RND), .in5(KBD), .out(DI), .sel(DI_SEL));  // open: in6, in7
  Register_File_2 register_file_1 (
    .Reset(rst), .RW(RW_REG), .DI(DI), .Clk(clk), .Stack_Pointer(SP), .A(rs), .B(rt), .HI_value(Hi_in),
    .LO_value(resultALU), .MD(en_md), .HI_value_2(Hi_out), .LO_value_2(Lo_out), .RA({A, TTY_DAta}), .RB(B),
    .DA(DA));
  assign bit_extender_2_out = {{16{offset[15]}}, offset};  // Bit_Extender bit_extender_2
  or or_2 (or_4_out[1], push, pop);
  Multiplexer #(.width(32), .enable("false")) multiplexer_4 (
    .in0({A, TTY_DAta}), .in1(SP), .out(multiplexer_4_out), .sel(or_3_out));
  or or_3 (or_3_out, push, pop);
  Multiplexer #(.select(2), .width(32), .enable("false")) multiplexer_5 (
    .in0(B), .in1(bit_extender_2_out), .in2(32'h4), .out(multiplexer_5_out), .sel(or_4_out));  // open: in3
  Multiplexer #(.select(2), .width(32), .enable("false")) multiplexer_6 (
    .in0(PC_prime), .in1(resultALU), .in2(SP), .in3({A, TTY_DAta}), .out(Mem_Addres), .sel(AddresSource));
  // Probe on {A, TTY_DAta}
  // Probe on B
  // Probe on multiplexer_4_out
  // Probe on multiplexer_5_out
  or or_4 (or_4_out[0], Store_Word, Arit_I, Load_Word);
  // Probe on AddresSource
  // Probe on mem_data
  // Probe on alu_1_result
  ALU_2 alu_1 (
    .A(multiplexer_4_out), .in_3(ALU_Selector), .RESULT(alu_1_result), .ZF(ZF), .NF(SF), .HIGH(Hi_in),
    .B(multiplexer_5_out));
  // Probe on ALU_Selector
  // Probe on Mem_Addres
  Register #(.width(32), .trigger("falling")) register_1 (
    .D(mem_data), .en(LoadInstruction), .Q(register_1_q), .clk(clk), .clr(rst));
  Register #(.width(32)) register_2 (.D(mem_data), .en(clk), .Q(Data), .clk(clk), .clr(rst));
  Multiplexer #(.width(32), .enable("false")) multiplexer_7 (.in0({A, TTY_DAta}), .in1(B), .out(Value), .sel(ValueSrc));
  // Probe on register_1_q
  // Probe on resultALU
  Register #(.width(32)) register_3 (.D(alu_1_result), .en(LoadResult), .Q(resultALU), .clk(clk), .clr(rst));
  ID id_1 (
    .Aritmetica(Arit), .Copy(Copia), .in_1(register_1_q), .is_add(add), .is_and(\and ), .is_slt(slt),
    .is_mfhi(mfhi), .is_beq(beq), .is_lw(Load_Word), .is_kbd(kbd_t), .rd(rd), .stack(Pila), .out_19(target),
    .is_sub(sub), .is_or(\or ), .is_sltu(sltu), .is_mflo(mflo), .is_bne(bne), .is_sw(Store_Word),
    .is_rnd(rnd_t), .rt(rt), .JMP(Salto), .is_mul(mult), .is_nor(\nor ), .is_slti(slti), .is_blez(blez),
    .is_push(push), .is_tty(tty), .rs(rs), .Inmediata(Arit_I), .fc(fc), .is_mulu(mulu), .is_xor(\xor ),
    .is_sltiu(sltiu), .is_bgtz(bgtz), .is_pop(pop), .is_halt(halt), .out_39(offset), .special(Especial),
    .is_div(div), .is_bltz(bltz), .oc(oc), .is_divu(divu), .is_andi(andi), .is_nop(nop), .is_ori(ori),
    .is_j(j), .is_addi(addi), .is_xori(xori), .is_jr(jr));
  or or_5 (sumi, addi, Store_Word, Load_Word);
  or or_6 (sum, add, pop);
  or or_7 (dif, sub, push, brf);
  ALU_Encoder alu_encoder_1 (
    .ALU_SEL(ALU_Selector), .is_add(sum), .is_and(\and ), .is_slt(slt), .is_sub(dif), .is_or(\or ),
    .is_sltu(sltu), .is_mul(mult), .is_nor(\nor ), .is_slti(slti), .is_mulu(mulu), .is_xor(\xor ),
    .is_sltiu(sltiu), .is_div(div), .is_andi(andi), .is_divu(divu), .is_ori(ori), .is_addi(sumi),
    .is_xori(xori));

  // Other names for the same wires on the sheet: A[6:0] = TTY_DAta; func_code[5:0] = fc; inm = Arit_I; lw = Load_Word;
  //   op_code[5:0] = oc; RW = RW_REG; sw = Store_Word; Value_Src = ValueSrc

  // Notes on the sheet:
  //   Input
  //   Output
endmodule

module Branch_Control (
  input  beq,
  input  ZF,
  input  j,
  input  [31:0] rs,
  input  bne,
  input  NF,
  input  jr,
  input  blez,
  input  [15:0] offset,
  input  bgtz,
  input  [31:0] pc_in,
  input  bltz,
  input  [25:0] target,
  output Is_Branch_flag,
  output [31:0] pc_out
);

  wire and_1_out, and_2_out, and_3_out, and_4_out, and_5_out, branch, gtz, lez, ltz, neq;
  wire [1:0] pc_selector;
  wire [31:0] bit_extender_1_out, branch_adress, pc_4, shifter_1_out;

  and and_1 (and_1_out, beq, ZF);
  and and_2 (and_2_out, bne, neq);
  and and_3 (and_3_out, blez, lez);
  and and_4 (and_4_out, bgtz, gtz);
  and and_5 (and_5_out, bltz, ltz);
  not not_1 (neq, ZF);
  or or_1 (lez, ZF, NF);
  and and_6 (gtz, ~ZF, ~NF);  // AND_Gate
  and and_7 (ltz, NF, ~ZF);  // AND_Gate
  or or_2 (branch, and_1_out, and_2_out, and_3_out, and_4_out, and_5_out);
  // Probe on pc_in[31:28]
  assign bit_extender_1_out = {{16{offset[15]}}, offset};  // Bit_Extender bit_extender_1
  Adder #(.width(32)) adder_1 (.a(32'h4), .b(pc_in), .out(pc_4));  // open: cin, cout
  Shifter #(.width(32)) shifter_1 (.in(bit_extender_1_out), .\dist (5'b00010), .out(shifter_1_out));
  Adder #(.width(32)) adder_2 (.a(pc_4), .b(shifter_1_out), .out(branch_adress));  // open: cin, cout
  // Probe on branch_adress
  or or_3 (Is_Branch_flag, beq, bne, blez, bgtz, bltz);
  // Probe on {pc_in[31:28], target, 2'b00}
  Multiplexer #(.select(2), .width(32), .enable("false")) multiplexer_1 (
    .in0(pc_4), .in1(branch_adress), .in2({pc_in[31:28], target, 2'b00}), .in3(rs), .out(pc_out),
    .sel(pc_selector));
  or or_4 (pc_selector[1], j, jr);
  or or_5 (pc_selector[0], jr, branch);
  // Probe on pc_selector

  // Other names for the same wires on the sheet: eq = ZF; j_adress[31:2] = {pc_in[31:28], target};
  //   pc_high[3:0] = pc_in[31:28]

  // Notes on the sheet:
  //   Input
endmodule

module Program_Counter (
  input  [31:0] in_1,
  input  clk,
  input  reset,
  input  enable,
  output [31:0] out_5
);

  Register #(.width(32)) PROGRAM_COUNTER (.D(in_1), .en(enable), .Q(out_5), .clk(clk), .clr(reset));

  // Other names for the same wires on the sheet: e = enable; pc_in[31:0] = in_1; pc_out[31:0] = out_5; rst = reset

  // Notes on the sheet:
  //   INPUT
  //   OUTPUT
endmodule

module ID (
  input  [31:0] in_1,
  output is_add,
  output is_and,
  output is_slt,
  output is_mfhi,
  output is_beq,
  output is_lw,
  output is_kbd,
  output [4:0] rd,
  output Aritmetica,
  output is_sub,
  output is_or,
  output is_sltu,
  output is_mflo,
  output is_bne,
  output is_sw,
  output is_rnd,
  output [4:0] rt,
  output [25:0] out_19,
  output Copy,
  output is_mul,
  output is_nor,
  output is_slti,
  output is_blez,
  output is_push,
  output is_tty,
  output [4:0] rs,
  output [5:0] fc,
  output is_mulu,
  output is_xor,
  output stack,
  output is_sltiu,
  output is_bgtz,
  output is_pop,
  output is_halt,
  output is_div,
  output JMP,
  output is_bltz,
  output [15:0] out_39,
  output [5:0] oc,
  output is_divu,
  output is_nop,
  output Inmediata,
  output is_addi,
  output is_andi,
  output is_j,
  output special,
  output is_ori,
  output is_jr,
  output is_xori
);

  wire and_1_out, and_3_out, comparator_1_eq, comparator_1_gt, comparator_2_lt, comparator_3_gt,
       comparator_4_lt, comparator_5_gt, comparator_6_lt, R;

  Comparator #(.width(6), .mode("unsigned")) comparator_1 (
    .a(in_1[31:26]), .b({6{1'b0}}), .gt(comparator_1_gt), .eq(comparator_1_eq));  // open: lt
  Comparator #(.width(6), .mode("unsigned")) comparator_2 (
    .a(in_1[5:0]), .b(6'b001001), .lt(comparator_2_lt));  // open: gt, eq
  Comparator #(.width(6), .mode("unsigned")) comparator_3 (
    .a(in_1[5:0]), .b(6'b001111), .gt(comparator_3_gt));  // open: eq, lt
  Comparator #(.width(6), .mode("unsigned")) comparator_4 (
    .a(in_1[5:0]), .b(6'b010011), .lt(comparator_4_lt));  // open: gt, eq
  Comparator #(.width(6), .mode("unsigned")) comparator_5 (
    .a(in_1[5:0]), .b(6'b010111), .gt(comparator_5_gt));  // open: eq, lt
  Comparator #(.width(6), .mode("unsigned")) comparator_6 (
    .a(in_1[31:26]), .b(6'b001000), .lt(comparator_6_lt));  // open: gt, eq
  and and_1 (and_1_out, comparator_6_lt, comparator_1_gt);
  and and_2 (special, in_1[26], in_1[27], in_1[28], in_1[29], in_1[30], in_1[31]);
  nor nor_1 (R, in_1[26], in_1[27], in_1[28], in_1[29], in_1[30], in_1[31]);
  or or_1 (JMP, and_1_out, and_3_out);
  and and_3 (and_3_out, comparator_1_eq, comparator_2_lt);
  and and_4 (Copy, comparator_1_eq, comparator_3_gt, comparator_4_lt);
  and and_5 (Aritmetica, comparator_1_eq, comparator_5_gt);
  and and_6 (stack, ~in_1[26], ~in_1[27], ~in_1[28], in_1[29], in_1[30], in_1[31]);  // AND_Gate
  and and_7 (is_j, ~in_1[26], in_1[27], ~in_1[28], ~in_1[29], ~in_1[30], ~in_1[31]);  // AND_Gate
  or or_2 (Inmediata, is_addi, is_slti, is_ori, is_sltiu, is_xori, is_andi);
  and and_8 (is_addi, ~in_1[26], ~in_1[27], ~in_1[28], in_1[29], ~in_1[30], ~in_1[31]);  // AND_Gate
  and and_9 (is_andi, ~in_1[26], ~in_1[27], in_1[28], in_1[29], ~in_1[30], ~in_1[31]);  // AND_Gate
  and and_10 (is_add, R, ~in_1[0], ~in_1[1], ~in_1[2], ~in_1[3], ~in_1[4], in_1[5]);  // AND_Gate
  and and_11 (is_sub, R, ~in_1[0], in_1[1], ~in_1[2], ~in_1[3], ~in_1[4], in_1[5]);  // AND_Gate
  and and_12 (is_mul, R, ~in_1[0], ~in_1[1], ~in_1[2], in_1[3], in_1[4], ~in_1[5]);  // AND_Gate
  and and_13 (is_mulu, R, in_1[0], ~in_1[1], ~in_1[2], in_1[3], in_1[4], ~in_1[5]);  // AND_Gate
  and and_14 (is_div, R, ~in_1[0], in_1[1], ~in_1[2], in_1[3], in_1[4], ~in_1[5]);  // AND_Gate
  and and_15 (is_divu, R, in_1[0], in_1[1], ~in_1[2], in_1[3], in_1[4], ~in_1[5]);  // AND_Gate
  and and_16 (is_ori, in_1[26], ~in_1[27], in_1[28], in_1[29], ~in_1[30], ~in_1[31]);  // AND_Gate
  and and_17 (is_xori, ~in_1[26], in_1[27], in_1[28], in_1[29], ~in_1[30], ~in_1[31]);  // AND_Gate
  and and_18 (is_slti, ~in_1[26], in_1[27], ~in_1[28], in_1[29], ~in_1[30], ~in_1[31]);  // AND_Gate
  and and_19 (is_sltiu, in_1[26], in_1[27], ~in_1[28], in_1[29], ~in_1[30], ~in_1[31]);  // AND_Gate
  and and_20 (is_and, R, ~in_1[0], ~in_1[1], in_1[2], ~in_1[3], ~in_1[4], in_1[5]);  // AND_Gate
  and and_21 (is_or, R, in_1[0], ~in_1[1], in_1[2], ~in_1[3], ~in_1[4], in_1[5]);  // AND_Gate
  and and_22 (is_nor, R, in_1[0], in_1[1], in_1[2], ~in_1[3], ~in_1[4], in_1[5]);  // AND_Gate
  and and_23 (is_xor, R, ~in_1[0], ~in_1[1], ~in_1[2], in_1[3], ~in_1[4], in_1[5]);  // AND_Gate
  and and_24 (is_beq, ~in_1[26], ~in_1[27], in_1[28], ~in_1[29], ~in_1[30], ~in_1[31]);  // AND_Gate
  and and_25 (is_bne, in_1[26], ~in_1[27], in_1[28], ~in_1[29], ~in_1[30], ~in_1[31]);  // AND_Gate
  and and_26 (is_blez, ~in_1[26], in_1[27], in_1[28], ~in_1[29], ~in_1[30], ~in_1[31]);  // AND_Gate
  and and_27 (is_bgtz, in_1[26], in_1[27], in_1[28], ~in_1[29], ~in_1[30], ~in_1[31]);  // AND_Gate
  and and_28 (is_bltz, in_1[26], ~in_1[27], ~in_1[28], ~in_1[29], ~in_1[30], ~in_1[31]);  // AND_Gate
  and and_29 (is_lw, in_1[26], in_1[27], ~in_1[28], ~in_1[29], ~in_1[30], in_1[31]);  // AND_Gate
  and and_30 (is_slt, R, ~in_1[0], in_1[1], ~in_1[2], in_1[3], ~in_1[4], in_1[5]);  // AND_Gate
  and and_31 (is_sltu, R, in_1[0], in_1[1], ~in_1[2], in_1[3], ~in_1[4], in_1[5]);  // AND_Gate
  and and_32 (is_nop, R, ~in_1[0], ~in_1[1], ~in_1[2], ~in_1[3], ~in_1[4], ~in_1[5]);  // AND_Gate
  and and_33 (is_sw, in_1[26], in_1[27], ~in_1[28], in_1[29], ~in_1[30], in_1[31]);  // AND_Gate
  and and_34 (is_mfhi, R, ~in_1[0], ~in_1[1], ~in_1[2], ~in_1[3], in_1[4], ~in_1[5]);  // AND_Gate
  and and_35 (is_mflo, R, ~in_1[0], in_1[1], ~in_1[2], ~in_1[3], in_1[4], ~in_1[5]);  // AND_Gate
  and and_36 (is_jr, R, ~in_1[0], ~in_1[1], ~in_1[2], in_1[3], ~in_1[4], ~in_1[5]);  // AND_Gate
  and and_37 (is_pop, stack, ~in_1[0], ~in_1[1], ~in_1[2], ~in_1[3], ~in_1[4], ~in_1[5]);  // AND_Gate
  and and_38 (is_push, stack, in_1[0], ~in_1[1], ~in_1[2], ~in_1[3], ~in_1[4], ~in_1[5]);  // AND_Gate
  and and_39 (is_halt, special, in_1[0], in_1[1], in_1[2], in_1[3], in_1[4], in_1[5]);
  and and_40 (is_tty, special, ~in_1[0], in_1[1], ~in_1[2], ~in_1[3], ~in_1[4], ~in_1[5]);  // AND_Gate
  and and_41 (is_kbd, special, ~in_1[0], ~in_1[1], in_1[2], ~in_1[3], ~in_1[4], ~in_1[5]);  // AND_Gate
  and and_42 (is_rnd, special, ~in_1[0], in_1[1], ~in_1[2], ~in_1[3], ~in_1[4], ~in_1[5]);  // AND_Gate

  assign fc = in_1[5:0];
  assign oc = in_1[31:26];
  assign out_19 = in_1[25:0];
  assign out_39 = in_1[15:0];
  assign rd = in_1[15:11];
  assign rs = in_1[25:21];
  assign rt = in_1[20:16];

  // Other names for the same wires on the sheet: add = is_add; addi = is_addi; and = is_and; andi = is_andi;
  //   beq = is_beq; bgtz = is_bgtz; blez = is_blez; bltz = is_bltz; bne = is_bne; div = is_div; divu = is_divu;
  //   halt = is_halt; f0 = in_1[0]; func_code[5:0] = in_1[5:0]; instruction[31:0] = in_1; offset[15:0] = in_1[15:0];
  //   target[25:0] = in_1[25:0]; f1 = in_1[1]; f2 = in_1[2]; f3 = in_1[3]; f4 = in_1[4]; f5 = in_1[5]; o0 = in_1[26];
  //   op_code[5:0] = in_1[31:26]; o1 = in_1[27]; o2 = in_1[28]; o3 = in_1[29]; o4 = in_1[30]; o5 = in_1[31]; j = is_j;
  //   jr = is_jr; kbd = is_kbd; lw = is_lw; mfhi = is_mfhi; mflo = is_mflo; mul = is_mul; mulu = is_mulu;
  //   nop = is_nop; nor = is_nor; or = is_or; ori = is_ori; pop = is_pop; push = is_push; rnd = is_rnd; slt = is_slt;
  //   slti = is_slti; sltiu = is_sltiu; sltu = is_sltu; sub = is_sub; sw = is_sw; tty = is_tty; xor = is_xor;
  //   xori = is_xori

  // Notes on the sheet:
  //   INPUT
  //   ARITMETICAS
  //   ALU
  //   &
  //   LOGICAS
  //   &
  //   COMPARACION
  //   OUTPUT
  //   COPIA A REGISTROS
  //   SALTO
  //   MEMORIA
  //   SPECIAL
  //   REGISTROS
  //   OTROS
endmodule

module _16_32_Sign_Extender (
  input  [15:0] in_1,
  output [31:0] Output
);

  Multiplexer #(.width(16)) multiplexer_1 (
    .in0({16{1'b0}}), .in1({16{1'b1}}), .out(Output[31:16]), .sel(in_1[15]));  // open: en

  assign Output[15:0] = in_1;

  // Notes on the sheet:
  //   SIGN EXTENDER
endmodule

module Control_Unit_2 (
  input  Clock,
  input  Ari,
  input  Especial,
  input  Load_Word,
  input  [3:0] R_Time,
  input  Copy,
  input  Store_Word,
  input  [3:0] W_time,
  input  Stack,
  input  rst,
  input  [5:0] fc,
  input  JMP,
  input  INM,
  input  [5:0] oc,
  output WrReg,
  output Enable_PC,
  output LOAD_RESULT,
  output TTY_Enable,
  output [1:0] ADDRESSOURCE,
  output Halt,
  output [1:0] SP_sel,
  output ValueSrc,
  output CS,
  output Kbd_Enable,
  output Write,
  output [2:0] DI_SEL,
  output Enable_Instruction
);

  wire A3Src_0a, A3Src_0b, A3Src_1a, A3Src_1b, AdrSrc_0a, AdrSrc_1a, AdrSrc_1b, ALUSrcB_1a, and_1_out,
       and_2_out, Arit_End, Arit_I_End, Copia_End, CS_a, d_ff_q, Decoded, demultiplexer_1_out0,
       demultiplexer_1_out1, demultiplexer_2_out1, demultiplexer_3_out0, demultiplexer_3_out1,
       demultiplexer_5_out0, demultiplexer_5_out1, demultiplexer_6_out0, Enable_instr_a, Enable_instr_b,
       Enable_PC_ari, Enable_PC_copy, Enable_PC_INM, Enable_PC_JMP, Enable_PC_lw, Enable_PC_special,
       Enable_PC_Stack, Enable_PC_sw, halt_t, IDLE_q, load_result_aritmeticas, load_result_inmediatas,
       load_result_lw, load_result_stack_0, load_result_stack_1, load_result_sw, or_1_out, or_2_out,
       or_3_out, or_4_out, or_5_out, or_6_out, or_13_out, or_16_out, or_22_out, reset_timer, rnd, Salto_End,
       SP_sel_t, timer_1_output, timer_2_output, timer_3_output, WD3Src_0a, WD3Src_0b, WD3Src_0d, WE3_a;

  and and_1 (and_1_out, Decoded, Stack);
  Demultiplexer #(.enable("false")) demultiplexer_1 (
    .out0(demultiplexer_1_out0), .out1(demultiplexer_1_out1), .in(and_1_out), .sel(fc[0]));
  or or_1 (or_1_out, or_5_out, demultiplexer_2_out1);
  or or_2 (or_2_out, demultiplexer_3_out0, demultiplexer_1_out0);
  D_Flip_Flop #(.trigger("falling")) IDLE (.clk(Clock), .D(or_1_out), .Q(IDLE_q), .preset(rst));  // open: Qn, en, reset
  D_Flip_Flop #(.trigger("falling")) Read_Ram (
    .clk(Clock), .D(or_2_out), .Q(AdrSrc_1a), .reset(rst));  // open: Qn, preset, en
  D_Flip_Flop #(.trigger("falling")) UpdPointer (
    .clk(Clock), .D(demultiplexer_1_out1), .Q(load_result_stack_1), .reset(rst));  // open: Qn, preset, en
  Demultiplexer #(.enable("false")) demultiplexer_2 (
    .out0(reset_timer), .out1(demultiplexer_2_out1), .in(IDLE_q), .sel(rst));
  Timer timer_1 (.in_1(R_Time), .in_2(Clock), .Output(timer_1_output), .in_3(Clock), .in_4(reset_timer));
  Tipo_Aritmeticas tipo_aritmeticas_1 (
    .Decoded(Decoded), .CLK(Clock), .ENABLE_PC(Enable_PC_ari), .func_code(fc), .rst(rst),
    .END_ARITMETICA(Arit_End), .Aritmetica(Ari), .LOAD_RESULT(load_result_aritmeticas), .WE3(WE3_a));
  Tipo_Salto tipo_salto_1 (
    .Decoded(Decoded), .Enable_PC(Enable_PC_JMP), .JMP(JMP), .END_JMP(Salto_End), .CLK(Clock), .rst(rst));
  Demultiplexer #(.enable("false")) demultiplexer_3 (
    .out0(demultiplexer_3_out0), .out1(demultiplexer_3_out1), .in(AdrSrc_1a), .sel(timer_1_output));
  or or_3 (or_3_out, Enable_instr_b, reset_timer);
  D_Flip_Flop #(.trigger("falling")) WR (
    .clk(Clock), .D(load_result_stack_1), .Q(A3Src_1b), .reset(rst));  // open: Qn, preset, en
  D_Flip_Flop #(.trigger("falling")) BuscInstr (
    .clk(Clock), .D(or_3_out), .Q(CS_a), .reset(rst));  // open: Qn, preset, en
  D_Flip_Flop #(.trigger("falling")) Write_Reg (
    .clk(Clock), .D(demultiplexer_3_out1), .Q(WD3Src_0b), .reset(rst));  // open: Qn, preset, en
  Demultiplexer #(.enable("false")) demultiplexer_4 (
    .out0(Enable_instr_b), .out1(Enable_instr_a), .in(CS_a), .sel(timer_2_output));
  Timer timer_2 (.in_1(R_Time), .in_2(Clock), .Output(timer_2_output), .in_3(Clock), .in_4(reset_timer));
  D_Flip_Flop #(.trigger("falling")) u_Decoded (
    .clk(Clock), .D(Enable_instr_a), .Q(Decoded), .reset(rst));  // open: Qn, preset, en
  D_Flip_Flop #(.trigger("falling")) UpdPointer_2 (
    .clk(Clock), .D(WD3Src_0b), .Q(load_result_stack_0), .reset(rst));  // open: Qn, preset, en
  or or_4 (or_4_out, demultiplexer_5_out0, A3Src_1b);
  D_Flip_Flop #(.trigger("falling")) W (.clk(Clock), .D(or_4_out), .Q(AdrSrc_1b), .reset(rst));  // open: Qn, preset, en
  or or_5 (or_5_out, Arit_End, Copia_End, Enable_PC_Stack, Salto_End, Arit_I_End, Enable_PC_special, Enable_PC_lw, Enable_PC_sw);
  Tipo_Inmediata tipo_inmediata_1 (
    .Decoded(Decoded), .CLK(Clock), .ENABLE_PC(Enable_PC_INM), .ALUSrcB(ALUSrcB_1a), .INM(INM), .rst(rst),
    .END_INM(Arit_I_End), .A3Src(A3Src_0a), .LOAD_RESULT(load_result_inmediatas));
  D_Flip_Flop #(.trigger("falling")) WR_2 (
    .clk(Clock), .D(load_result_stack_0), .Q(A3Src_1a), .reset(rst));  // open: Qn, preset, en
  Tipo_Copia tipo_copia_1 (
    .Decoded(Decoded), .CLK(Clock), .ENABLE_PC(Enable_PC_copy), .func_code(fc), .rst(rst),
    .END_COPIA(Copia_End), .Copia(Copy), .WD3SRC0(WD3Src_0a), .WD3SRC1(DI_SEL[1]));
  Timer timer_3 (.in_1(W_time), .in_2(Clock), .Output(timer_3_output), .in_3(Clock), .in_4(reset_timer));
  Demultiplexer #(.enable("false")) demultiplexer_5 (
    .out0(demultiplexer_5_out0), .out1(demultiplexer_5_out1), .in(AdrSrc_1b), .sel(timer_3_output));
  or or_6 (or_6_out, A3Src_1a, demultiplexer_5_out1);
  D_Flip_Flop #(.trigger("falling")) END_PILA (
    .clk(Clock), .D(or_6_out), .Q(Enable_PC_Stack), .reset(rst));  // open: Qn, preset, en
  or or_7 (SP_sel_t, load_result_stack_0, load_result_stack_1);
  or or_8 (Enable_Instruction, Enable_instr_a, Enable_instr_b);
  or or_9 (Write, AdrSrc_1b, ValueSrc);
  or or_10 (CS, CS_a, AdrSrc_1a, AdrSrc_1b, AdrSrc_0a, ValueSrc);
  or or_11 (Enable_PC, Enable_PC_ari, Enable_PC_copy, Enable_PC_JMP, Enable_PC_INM, Enable_PC_Stack, Enable_PC_lw, Enable_PC_sw, Enable_PC_special);
  Tipo_sw tipo_sw_1 (
    .END_SW(Enable_PC_sw), .Decoded(Decoded), .CLK(Clock), .sw(Store_Word), .rst(rst),
    .LOAD_RESULT(load_result_sw), .W_Time(W_time), .reset_timer(reset_timer), .Value_Src(ValueSrc));
  Tipo_lw tipo_lw_1 (
    .END_LW(Enable_PC_lw), .Decoded(Decoded), .CLK(Clock), .rst(rst), .LOAD_RESULT(load_result_lw),
    .lw(Load_Word), .reset_timer(reset_timer), .AdrSrc_0a(AdrSrc_0a), .R_Time(R_Time), .A3Src_0b(A3Src_0b));
  or or_12 (DI_SEL[2], rnd, Kbd_Enable);
  Demultiplexer #(.enable("false")) demultiplexer_6 (
    .out0(demultiplexer_6_out0), .out1(WD3Src_0d), .in(DI_SEL[2]), .sel(Kbd_Enable));
  or or_13 (or_13_out, demultiplexer_6_out0, WD3Src_0d);
  or or_14 (LOAD_RESULT, load_result_aritmeticas, load_result_inmediatas, load_result_stack_0, load_result_stack_1, load_result_lw, load_result_sw);
  or or_15 (WrReg, WE3_a, A3Src_0a, A3Src_1a, A3Src_1b, A3Src_0b, DI_SEL[2], WD3Src_0b, DI_SEL[1]);
  or or_16 (or_16_out, or_13_out, TTY_Enable);
  D_Flip_Flop #(.trigger("falling")) special_End (
    .clk(Clock), .D(or_16_out), .Q(Enable_PC_special), .reset(rst));  // open: Qn, preset, en
  or or_17 (SP_sel[0], A3Src_0a, A3Src_0b);
  or or_18 (ADDRESSOURCE[0], AdrSrc_0a, ValueSrc);
  or or_19 (DI_SEL[0], WD3Src_0a, WD3Src_0b, A3Src_0b, WD3Src_0d);
  and and_2 (and_2_out, Decoded, Especial);
  D_Flip_Flop #(.trigger("falling")) d_ff (
    .clk(Clock), .D(and_2_out), .Q(d_ff_q), .reset(rst));  // open: Qn, preset, en
  or or_20 (ADDRESSOURCE[1], AdrSrc_1a, AdrSrc_1b);
  or or_21 (SP_sel[1], A3Src_1a, A3Src_1b);
  Demultiplexer #(.select(2), .enable("false")) demultiplexer_7 (
    .out0(TTY_Enable), .out1(rnd), .out2(Kbd_Enable), .out3(halt_t), .in(d_ff_q), .sel(fc[2:1]));
  D_Flip_Flop #(.trigger("falling")) Finish_Program (
    .clk(Clock), .D(or_22_out), .Q(Halt), .reset(rst));  // open: Qn, preset, en
  or or_22 (or_22_out, Halt, halt_t);

  // Other names for the same wires on the sheet: A3Src[1:0] = SP_sel; A3Src_0 = SP_sel[0]; A3Src_1 = SP_sel[1];
  //   AdrSrc[1:0] = ADDRESSOURCE; AdrSrc_0 = ADDRESSOURCE[0]; AdrSrc_1 = ADDRESSOURCE[1]; Aritmetica = Ari;
  //   CLK = Clock; CS_b = AdrSrc_1a; CS_d = AdrSrc_0a; Especial_End = Enable_PC_special; func_code[5:0] = fc;
  //   kbd = Kbd_Enable; SP_1 = load_result_stack_0; SP_2 = load_result_stack_1; lw = Load_Word; lw_End = Enable_PC_lw;
  //   op_code[5:0] = oc; Pila_End = Enable_PC_Stack; Stop = Halt; sw = Store_Word; Sw_End = Enable_PC_sw;
  //   tty = TTY_Enable; WD3Src[2:0] = DI_SEL; WD3Src_0 = DI_SEL[0]; WD3Src_1a = DI_SEL[1]; WE3_h = DI_SEL[1];
  //   WD3Src_2 = DI_SEL[2]; WE3_f = DI_SEL[2]; WE3 = WrReg; WE3_b = A3Src_0a; WE3_c = A3Src_1a; WE3_d = A3Src_1b;
  //   WD3Src_0c = A3Src_0b; WE3_e = A3Src_0b; WE3_g = WD3Src_0b; CS_c = AdrSrc_1b; Write_a = AdrSrc_1b;
  //   AdrSrc_0b = ValueSrc; CS_e = ValueSrc; Value_Src = ValueSrc; Write_b = ValueSrc

  // Notes on the sheet:
  //   TIPO ARITMETICAS
  //   TIPO SALTO
  //   INPUT 
  //   TIPO STACK
  //   OUTPUT 
  //   TIPO COPIA
  //   TIPO INMEDIATAS
  //   TIPO SW
  //   TIPO LW
  //   TIPO SPECIAL
endmodule

module Tipo_Aritmeticas (
  input  Decoded,
  input  CLK,
  input  [5:0] func_code,
  input  rst,
  input  Aritmetica,
  output ENABLE_PC,
  output END_ARITMETICA,
  output LOAD_RESULT,
  output WE3
);

  wire and_1_out, and_2_out, comparator_1_gt, comparator_2_lt, demultiplexer_1_out0, demultiplexer_1_out1,
       or_1_out;

  and and_1 (and_1_out, Decoded, Aritmetica);
  Comparator #(.width(6)) comparator_1 (.a(func_code), .b(6'b010011), .gt(comparator_1_gt));  // open: eq, lt
  Comparator #(.width(6)) comparator_2 (.a(func_code), .b(6'b011100), .lt(comparator_2_lt));  // open: gt, eq
  D_Flip_Flop #(.trigger("falling")) d_ff (
    .clk(CLK), .D(and_1_out), .Q(LOAD_RESULT), .reset(rst));  // open: Qn, preset, en
  and and_2 (and_2_out, comparator_1_gt, comparator_2_lt);
  Demultiplexer #(.enable("false")) demultiplexer_1 (
    .out0(demultiplexer_1_out0), .out1(demultiplexer_1_out1), .in(LOAD_RESULT), .sel(and_2_out));
  D_Flip_Flop #(.trigger("falling")) WR (
    .clk(CLK), .D(demultiplexer_1_out0), .Q(WE3), .reset(rst));  // open: Qn, preset, en
  or or_1 (or_1_out, WE3, demultiplexer_1_out1);
  D_Flip_Flop #(.trigger("falling")) Finish (
    .clk(CLK), .D(or_1_out), .Q(ENABLE_PC), .reset(rst));  // open: Qn, preset, en

  assign END_ARITMETICA = ENABLE_PC;

  // Notes on the sheet:
  //   INPUT
  //   TIPO ARITMETICAS
  //   OUTPUT
endmodule

module Tipo_Copia (
  input  Decoded,
  input  CLK,
  input  [5:0] func_code,
  input  rst,
  input  Copia,
  output ENABLE_PC,
  output END_COPIA,
  output WD3SRC0,
  output WD3SRC1
);

  wire and_1_out, comparator_1_eq, demultiplexer_1_out1, or_1_out;

  D_Flip_Flop #(.trigger("falling")) d_ff (.clk(CLK), .D(and_1_out), .Q(WD3SRC1), .reset(rst));  // open: Qn, preset, en
  and and_1 (and_1_out, Decoded, Copia);
  Comparator #(.width(6)) comparator_1 (.a(func_code), .b(6'b010000), .eq(comparator_1_eq));  // open: gt, lt
  Demultiplexer #(.enable("false")) demultiplexer_1 (
    .out0(WD3SRC0), .out1(demultiplexer_1_out1), .in(WD3SRC1), .sel(comparator_1_eq));
  or or_1 (or_1_out, WD3SRC0, demultiplexer_1_out1);
  D_Flip_Flop #(.trigger("falling")) Finish (
    .clk(CLK), .D(or_1_out), .Q(ENABLE_PC), .reset(rst));  // open: Qn, preset, en

  assign END_COPIA = ENABLE_PC;

  // Notes on the sheet:
  //   INPUT
  //   TIPO COPIA
  //   OUTPUT
endmodule

module Tipo_Salto (
  input  Decoded,
  input  JMP,
  input  CLK,
  input  rst,
  output Enable_PC,
  output END_JMP
);

  wire and_1_out;

  and and_1 (and_1_out, Decoded, JMP);
  D_Flip_Flop #(.trigger("falling")) d_ff (
    .clk(CLK), .D(and_1_out), .Q(Enable_PC), .reset(rst));  // open: Qn, preset, en
  D_Flip_Flop #(.trigger("falling")) Finish (
    .clk(CLK), .D(Enable_PC), .Q(END_JMP), .reset(rst));  // open: Qn, preset, en

  // Notes on the sheet:
  //   INPUT
  //   TIPO SALTO
  //   OUTPUT
endmodule

module Tipo_sw (
  input  Decoded,
  input  CLK,
  input  sw,
  input  rst,
  input  [3:0] W_Time,
  input  reset_timer,
  output END_SW,
  output LOAD_RESULT,
  output Value_Src
);

  wire and_1_out, demultiplexer_1_out0, demultiplexer_1_out1, or_1_out, timer_1_output;

  and and_1 (and_1_out, Decoded, sw);
  D_Flip_Flop #(.trigger("falling")) d_ff (
    .clk(CLK), .D(and_1_out), .Q(LOAD_RESULT), .reset(rst));  // open: Qn, preset, en
  or or_1 (or_1_out, demultiplexer_1_out0, LOAD_RESULT);
  D_Flip_Flop #(.trigger("falling")) Write (
    .clk(CLK), .D(or_1_out), .Q(Value_Src), .reset(rst));  // open: Qn, preset, en
  Timer timer_1 (.in_1(W_Time), .in_2(CLK), .Output(timer_1_output), .in_3(CLK), .in_4(reset_timer));
  Demultiplexer #(.enable("false")) demultiplexer_1 (
    .out0(demultiplexer_1_out0), .out1(demultiplexer_1_out1), .in(Value_Src), .sel(timer_1_output));
  D_Flip_Flop #(.trigger("falling")) Finish (
    .clk(CLK), .D(demultiplexer_1_out1), .Q(END_SW), .reset(rst));  // open: Qn, preset, en

  // Notes on the sheet:
  //   TIPO SW
  //   INPUT
  //   OUTPUT
endmodule

module Tipo_lw (
  input  Decoded,
  input  CLK,
  input  lw,
  input  rst,
  input  [3:0] R_Time,
  input  reset_timer,
  output END_LW,
  output LOAD_RESULT,
  output AdrSrc_0a,
  output A3Src_0b
);

  wire and_1_out, demultiplexer_1_out0, demultiplexer_1_out1, or_1_out, timer_1_output;

  and and_1 (and_1_out, Decoded, lw);
  D_Flip_Flop #(.trigger("falling")) d_ff (
    .clk(CLK), .D(and_1_out), .Q(LOAD_RESULT), .reset(rst));  // open: Qn, preset, en
  or or_1 (or_1_out, demultiplexer_1_out0, LOAD_RESULT);
  D_Flip_Flop #(.trigger("falling")) Read_Ram (
    .clk(CLK), .D(or_1_out), .Q(AdrSrc_0a), .reset(rst));  // open: Qn, preset, en
  Timer timer_1 (.in_1(R_Time), .in_2(CLK), .Output(timer_1_output), .in_3(CLK), .in_4(reset_timer));
  Demultiplexer #(.enable("false")) demultiplexer_1 (
    .out0(demultiplexer_1_out0), .out1(demultiplexer_1_out1), .in(AdrSrc_0a), .sel(timer_1_output));
  D_Flip_Flop #(.trigger("falling")) WR (
    .clk(CLK), .D(demultiplexer_1_out1), .Q(A3Src_0b), .reset(rst));  // open: Qn, preset, en
  D_Flip_Flop #(.trigger("falling")) Finish (.clk(CLK), .D(A3Src_0b), .Q(END_LW), .reset(rst));  // open: Qn, preset, en

  // Notes on the sheet:
  //   INPUT
  //   TIPO LW
  //   OUTPUT
endmodule

module Tipo_Inmediata (
  input  Decoded,
  input  CLK,
  input  INM,
  input  rst,
  output ENABLE_PC,
  output ALUSrcB,
  output END_INM,
  output A3Src,
  output LOAD_RESULT
);

  wire and_1_out;

  and and_1 (and_1_out, Decoded, INM);
  D_Flip_Flop #(.trigger("falling")) d_ff (.clk(CLK), .D(and_1_out), .Q(ALUSrcB), .reset(rst));  // open: Qn, preset, en
  D_Flip_Flop #(.trigger("falling")) WR (.clk(CLK), .D(ALUSrcB), .Q(A3Src), .reset(rst));  // open: Qn, preset, en
  D_Flip_Flop #(.trigger("falling")) Finish (.clk(CLK), .D(A3Src), .Q(ENABLE_PC), .reset(rst));  // open: Qn, preset, en

  assign END_INM = ENABLE_PC;
  assign LOAD_RESULT = ALUSrcB;

  // Notes on the sheet:
  //   INPUT
  //   TIPO INMEDIATAS
  //   OUTPUT
endmodule

module Timer (
  input  [3:0] in_1,
  input  in_2,
  input  in_3,
  input  in_4,
  output Output
);

  wire [3:0] counter_1_q;

  Counter #(.width(4), .max('hf)) counter_1 (
    .count(in_2), .Q(counter_1_q), .clk(in_3), .clr(in_4));  // open: load, D, carry
  Comparator #(.width(4)) comparator_1 (.a(in_1), .b(counter_1_q), .eq(Output));  // open: gt, lt
endmodule

module ABS (
  input  [31:0] A,
  output [31:0] A_2
);

  wire [31:0] and_1_out, and_2_out, EXT_Sign_A, negator_1_out, not_1_out;

  assign EXT_Sign_A = {{31{A[31]}}, A[31]};  // Bit_Extender bit_extender_1
  // Probe on A
  Negator #(.width(32)) negator_1 (.in(A), .out(negator_1_out));
  // Probe on A_2
  assign and_1_out = EXT_Sign_A & negator_1_out;  // AND_Gate and_1, 32 bits wide
  assign not_1_out = ~EXT_Sign_A;  // NOT_Gate not_1, 32 bits wide
  assign and_2_out = not_1_out & A;  // AND_Gate and_2, 32 bits wide
  assign A_2 = and_1_out | and_2_out;  // OR_Gate or_1, 32 bits wide

  // Other names for the same wires on the sheet: Sign_A = A[31]; A_t[31:0] = A_2

  // Notes on the sheet:
  //   INPUT
  //   OUTPUT
endmodule

module ALU_Encoder (
  input  is_add,
  input  is_and,
  input  is_slt,
  input  is_sub,
  input  is_or,
  input  is_sltu,
  input  is_mul,
  input  is_nor,
  input  is_slti,
  input  is_mulu,
  input  is_xor,
  input  is_sltiu,
  input  is_div,
  input  is_andi,
  input  is_divu,
  input  is_ori,
  input  is_addi,
  input  is_xori,
  output [3:0] ALU_SEL
);

  wire or_1_out, or_2_out, or_3_out, or_4_out, or_5_out, or_6_out;
  wire [3:0] and_1_out, and_2_out, and_3_out, and_4_out, and_5_out, and_6_out, and_7_out, and_8_out,
       and_9_out, and_10_out, and_11_out, and_12_out, bit_extender_1_out, bit_extender_2_out,
       bit_extender_3_out, bit_extender_4_out, bit_extender_5_out, bit_extender_6_out, bit_extender_7_out,
       bit_extender_8_out, bit_extender_9_out, bit_extender_10_out, bit_extender_11_out, bit_extender_12_out;

  or or_1 (or_1_out, is_add, is_addi);
  or or_2 (or_2_out, is_and, is_andi);
  or or_3 (or_3_out, is_or, is_ori);
  or or_4 (or_4_out, is_xor, is_xori);
  or or_5 (or_5_out, is_slt, is_slti);
  or or_6 (or_6_out, is_sltu, is_sltiu);
  assign bit_extender_1_out = {{3{or_1_out}}, or_1_out};  // Bit_Extender bit_extender_1
  assign bit_extender_2_out = {{3{is_sub}}, is_sub};  // Bit_Extender bit_extender_2
  assign bit_extender_3_out = {{3{is_nor}}, is_nor};  // Bit_Extender bit_extender_3
  assign bit_extender_4_out = {{3{is_mul}}, is_mul};  // Bit_Extender bit_extender_4
  assign bit_extender_5_out = {{3{is_mulu}}, is_mulu};  // Bit_Extender bit_extender_5
  assign bit_extender_6_out = {{3{is_div}}, is_div};  // Bit_Extender bit_extender_6
  assign bit_extender_7_out = {{3{is_divu}}, is_divu};  // Bit_Extender bit_extender_7
  assign bit_extender_8_out = {{3{or_2_out}}, or_2_out};  // Bit_Extender bit_extender_8
  assign bit_extender_9_out = {{3{or_3_out}}, or_3_out};  // Bit_Extender bit_extender_9
  assign bit_extender_10_out = {{3{or_4_out}}, or_4_out};  // Bit_Extender bit_extender_10
  assign bit_extender_11_out = {{3{or_5_out}}, or_5_out};  // Bit_Extender bit_extender_11
  assign bit_extender_12_out = {{3{or_6_out}}, or_6_out};  // Bit_Extender bit_extender_12
  assign and_1_out = bit_extender_1_out & 4'b0001;  // AND_Gate and_1, 4 bits wide
  assign and_2_out = bit_extender_2_out & 4'b0010;  // AND_Gate and_2, 4 bits wide
  assign and_3_out = bit_extender_3_out & 4'b0011;  // AND_Gate and_3, 4 bits wide
  assign and_4_out = bit_extender_4_out & 4'b0100;  // AND_Gate and_4, 4 bits wide
  assign and_5_out = bit_extender_5_out & 4'b0101;  // AND_Gate and_5, 4 bits wide
  assign and_6_out = bit_extender_6_out & 4'b0110;  // AND_Gate and_6, 4 bits wide
  assign and_7_out = bit_extender_7_out & 4'b0111;  // AND_Gate and_7, 4 bits wide
  assign and_8_out = bit_extender_8_out & 4'b1000;  // AND_Gate and_8, 4 bits wide
  assign and_9_out = bit_extender_9_out & 4'b1001;  // AND_Gate and_9, 4 bits wide
  assign and_10_out = bit_extender_10_out & 4'b1010;  // AND_Gate and_10, 4 bits wide
  assign and_11_out = bit_extender_11_out & 4'b1011;  // AND_Gate and_11, 4 bits wide
  assign and_12_out = bit_extender_12_out & 4'b1100;  // AND_Gate and_12, 4 bits wide
  assign ALU_SEL = and_1_out | and_2_out | and_3_out | and_4_out | and_5_out | and_6_out | and_7_out | and_8_out | and_9_out | and_10_out | and_11_out | and_12_out;  // OR_Gate or_7, 4 bits wide

  // Other names for the same wires on the sheet: add = is_add; addi = is_addi; and = is_and; andi = is_andi;
  //   div = is_div; divu = is_divu; mul = is_mul; mulu = is_mulu; nor = is_nor; or = is_or; ori = is_ori;
  //   slt = is_slt; slti = is_slti; sltiu = is_sltiu; sltu = is_sltu; sub = is_sub; xor = is_xor; xori = is_xori

  // Notes on the sheet:
  //   OUTPUT
  //   INPUT 
  //   Operacion 
  //   add
  //   sub
  //   nor
  //   mul
  //   mulu
  //   div
  //   divu
  //   and
  //   or
  //   xor
  //   slt
  //   sltu
  //   Codigo
  //   0001
  //   0010
  //   0011
  //   0100
  //   0101
  //   0110
  //   0111
  //   1000
  //   1001
  //   1010
  //   1011
  //   1100
endmodule

module ALU_2 (
  input  [31:0] A,
  input  [31:0] B,
  input  [3:0] in_3,
  output ZF,
  output [31:0] RESULT,
  output NF,
  output [31:0] HIGH
);

  wire comparator_1_lt, comparator_2_lt, HI_EN, not_1_out;
  wire [31:0] AND, DIV, DIV_HIGH, DIVU, DIVU_HIGH, MUL, MUL_HIGH, MULU, MULU_HIGH, NOR, OR, SLT, SLTU, SUB,
       SUM, undriven, XOR;

  Adder #(.width(32)) adder_1 (.a(A), .b(B), .out(SUM));  // open: cin, cout
  Subtractor #(.width(32)) subtractor_1 (.a(A), .b(B), .out(SUB));  // open: bin, bout
  Comparator #(.width(32)) comparator_1 (.a(A), .b(B), .lt(comparator_1_lt));  // open: gt, eq
  Comparator #(.width(32), .mode("unsigned")) comparator_2 (.a(A), .b(B), .lt(comparator_2_lt));  // open: gt, eq
  assign SLT = {{31{1'b0}}, comparator_1_lt};  // Bit_Extender bit_extender_1
  assign SLTU = {{31{1'b0}}, comparator_2_lt};  // Bit_Extender bit_extender_2
  assign AND = A & B;  // AND_Gate and_1, 32 bits wide
  assign NOR = ~(A | B);  // NOR_Gate nor_1, 32 bits wide
  assign XOR = A ^ B;  // XOR_Gate xor_1, 32 bits wide
  assign OR = A | B;  // OR_Gate or_1, 32 bits wide
  MULU mulu_1 (.A(A), .B(B), .L(MULU), .H(MULU_HIGH));
  DIVU divu_1 (.A(A), .B(B), .L(DIVU), .H(DIVU_HIGH));
  Multiplier #(.width(32)) multiplier_1 (.a(A), .b(B), .out(MUL), .cout(MUL_HIGH));  // open: cin
  Divider #(.width(32)) divider_1 (.a(A), .b(B), .out(DIV), .rem(DIV_HIGH));  // open: upper
  Multiplexer #(.select(2), .width(32)) multiplexer_1 (
    .in0(MUL_HIGH), .in1(MULU_HIGH), .in2(DIV_HIGH), .in3(DIVU_HIGH), .out(HIGH), .sel(in_3[1:0]), .en(HI_EN));
  not not_1 (not_1_out, in_3[3]);
  and and_2 (HI_EN, in_3[2], not_1_out);
  // Probe on A
  Multiplexer #(.select(4), .width(32), .disabled(0), .enable("false")) multiplexer_2 (
    .in0(A), .in1(SUM), .in2(SUB), .in3(NOR), .in4(MUL), .in5(MULU), .in6(DIV), .in7(DIVU), .in8(AND),
    .in9(OR), .in10(XOR), .in11(SLT), .in12(SLTU), .in13(undriven), .out(RESULT), .sel(in_3));  // open: in14, in15
  // Probe on RESULT
  Comparator #(.width(32)) comparator_3 (.a(RESULT), .b({32{1'b0}}), .eq(ZF), .lt(NF));  // open: gt

  // Other names for the same wires on the sheet: HI_S[1:0] = in_3[1:0]; Selector[3:0] = in_3; B2 = in_3[2];
  //   B3 = in_3[3]

  // Notes on the sheet:
  //   INPUT
  //   OPS
  //   OUTPUT
endmodule

module MULU (
  input  [31:0] A,
  input  [31:0] B,
  output [31:0] L,
  output [31:0] H
);

  wire [31:0] abs_1_a_2, abs_2_a_2;

  ABS abs_1 (.A(A), .A_2(abs_1_a_2));
  ABS abs_2 (.A(B), .A_2(abs_2_a_2));
  Multiplier #(.width(32)) multiplier_1 (.a(abs_1_a_2), .b(abs_2_a_2), .out(L), .cout(H));  // open: cin

  // Other names for the same wires on the sheet: MULU_HIGH[31:0] = H; MULU_LOW[31:0] = L

  // Notes on the sheet:
  //   INPUT
  //   OUTPUT
endmodule

module DIVU (
  input  [31:0] A,
  input  [31:0] B,
  output [31:0] L,
  output [31:0] H
);

  wire [31:0] abs_1_a_2, abs_2_a_2;

  ABS abs_1 (.A(A), .A_2(abs_1_a_2));
  ABS abs_2 (.A(B), .A_2(abs_2_a_2));
  Divider #(.width(32)) divider_1 (.a(abs_1_a_2), .b(abs_2_a_2), .out(L), .rem(H));  // open: upper

  // Other names for the same wires on the sheet: DIVU_HIGH[31:0] = H; DIVU_LOW[31:0] = L

  // Notes on the sheet:
  //   INPUT
  //   OUTPUT
endmodule

module ReadInstruction (
  input  [31:0] BANK0,
  input  [31:0] BANK1,
  input  [31:0] BANK2,
  input  [31:0] BANK3,
  input  [31:0] MEMORY,
  output [31:0] RAM_DATA
);

  Multiplexer #(.select(2), .width(32), .enable("false")) multiplexer_1 (
    .in0(BANK0), .in1(BANK1), .in2(BANK2), .in3(BANK3),
    .out({RAM_DATA[7:0], RAM_DATA[15:8], RAM_DATA[23:16], RAM_DATA[31:24]}), .sel(MEMORY[3:2]));

  // Other names for the same wires on the sheet: SELECTOR[1:0] = MEMORY[3:2]
endmodule

module WriteRam (
  input  [31:0] MEMORY,
  input  [31:0] VALUE,
  output [3:0] MASK,
  output [31:0] INPUT0,
  output [15:0] ADDRESS,
  output [31:0] INPUT1,
  output [31:0] INPUT2,
  output [31:0] INPUT3
);

  Demultiplexer #(.select(2), .enable("false")) demultiplexer_1 (
    .out0(MASK[0]), .out1(MASK[1]), .out2(MASK[2]), .out3(MASK[3]), .in(1'b1), .sel(MEMORY[3:2]));
  Demultiplexer #(.select(2), .width(32), .enable("false")) demultiplexer_2 (
    .out0(INPUT0), .out1(INPUT1), .out2(INPUT2), .out3(INPUT3),
    .in({VALUE[7:0], VALUE[15:8], VALUE[23:16], VALUE[31:24]}), .sel(MEMORY[3:2]));

  assign ADDRESS = MEMORY[19:4];

  // Other names for the same wires on the sheet: SELECTOR[1:0] = MEMORY[3:2]
endmodule
